# Fritzing sketch rc_perfboard2 (saved by Fritzing 0.9.3b)
perfboards: 12

parts:
  IC1 = L293D [package=THT]
  Part1 = Arduino Nano (Rev3.0)
  J1 = JST XH 2A male [form="♂ (male)" package=THT]
  J2 = JST XH 2A male [form="♂ (male)" package=THT]
  J3 = JST XH 2A male [form="♂ (male)" package=THT]
  J4 = JST XH 2A male [form="♂ (male)" package=THT]
  J5 = JST XH 2A male [form="♂ (male)" package=THT]
  IC2 = L293D [package=THT]
  Part3 = NRF24L01+ Breakout Board
  IC3 = L293D [package=THT]
  IC4 = L293D [package=THT]
  Part4 = Arduino Nano (Rev3.0)
  J6 = JST XH 2A male [form="♂ (male)" package=THT]
  J7 = JST XH 2A male [form="♂ (male)" package=THT]
  J8 = JST XH 2A male [form="♂ (male)" package=THT]
  J9 = JST XH 2A male [form="♂ (male)" package=THT]
  J10 = JST XH 2A male [form="♂ (male)" package=THT]
  J11 = JST XH 2A male [form="♂ (male)" package=THT]
  J12 = JST XH 2A male [form="♂ (male)" package=THT]
  J13 = JST XH 2A male [form="♂ (male)" package=THT]
  J14 = JST XH 2A male [form="♂ (male)" package=THT]
  IC5 = L293D [package=THT]
  IC6 = L293D [package=THT]
  J15 = JST XH 2A male [form="♂ (male)" package=THT]
  J16 = JST XH 2A male [form="♂ (male)" package=THT]  # not connected
  WeMos_D1_Mini1 = WeMos D1 Mini
  Part5 = NRF24L01+ Breakout Board  # not connected

nets:
  N1: IC1.Enable_1, Part1.D3
  N2: IC1.In_1, Part1.D2
  N3: IC1.Out_1_(_Controlled_by_Enable_1_), J2.pin1
  N4: IC1.0V, Part1.GND, IC2.0V
  N5: IC1.Out_2_(_Controlled_by_Enable_1_), J2.pin2
  N6: IC1.In_2, Part1.D5
  N7: IC1.+Vmotor, J5.pin2, IC2.+Vmotor
  N8: IC1.Out_3_(_Controlled_by_Enable_2_), J1.pin2
  N9: IC1.Out_4_(_Controlled_by_Enable_2_), J1.pin1
  N10: IC1.+V, Part1.5V, IC2.+V
  N11: Part1.D6, IC2.Enable_2
  N12: Part1.A5, IC2.In_1, IC2.In_4
  N13: Part1.A0, IC2.In_2, IC2.In_3
  N14: J3.pin1, IC2.Out_3_(_Controlled_by_Enable_2_)
  N15: J3.pin2, IC2.Out_4_(_Controlled_by_Enable_2_)
  N16: J4.pin1, IC2.Out_2_(_Controlled_by_Enable_1_)
  N17: J4.pin2, IC2.Out_1_(_Controlled_by_Enable_1_)
  VCC: Part3.VCC, Part4.3V3
  N18: Part3.CE, Part4.D7
  N19: Part3.CS, Part4.D8
  N20: Part3.SCK, Part4.D13/SCK
  N21: Part3.MOSI, Part4.D11/MOSI
  N22: Part3.MISO, Part4.D12/MISO
  N23: IC3.Enable_1, Part4.D5
  N24: IC3.In_1, IC3.In_2, Part4.A5
  N25: IC3.Out_1_(_Controlled_by_Enable_1_), J6.pin2
  N26: IC3.0V, IC4.0V, Part4.GND, J10.pin1
  N27: IC3.Out_2_(_Controlled_by_Enable_1_), J6.pin1
  N28: IC3.+Vmotor, IC4.+Vmotor, Part4.VIN, J10.pin2
  N29: IC3.Enable_2, Part4.D6
  N30: IC3.In_3, IC3.In_4, Part4.A0
  N31: IC3.Out_3_(_Controlled_by_Enable_2_), J7.pin1
  N32: IC3.Out_4_(_Controlled_by_Enable_2_), J7.pin2
  N33: IC3.+V, IC4.+V, Part4.5V
  N34: IC4.Enable_1, Part4.D9
  N35: IC4.In_1, IC4.In_4, Part4.D3
  N36: IC4.Out_1_(_Controlled_by_Enable_1_), J9.pin2
  N37: IC4.Out_2_(_Controlled_by_Enable_1_), J9.pin1
  N38: IC4.In_2, IC4.In_3, Part4.D4
  N39: IC4.Enable_2, Part4.D10
  N40: IC4.Out_3_(_Controlled_by_Enable_2_), J8.pin2
  N41: IC4.Out_4_(_Controlled_by_Enable_2_), J8.pin1
  N42: J11.pin1, IC5.Out_3_(_Controlled_by_Enable_2_)
  N43: J11.pin2, IC5.Out_4_(_Controlled_by_Enable_2_)
  N44: J12.pin1, IC5.Out_2_(_Controlled_by_Enable_1_)
  N45: J12.pin2, IC5.Out_1_(_Controlled_by_Enable_1_)
  N46: J13.pin1, IC6.Out_2_(_Controlled_by_Enable_1_)
  N47: J13.pin2, IC6.Out_1_(_Controlled_by_Enable_1_)
  N48: J14.pin1, IC6.Out_3_(_Controlled_by_Enable_2_)
  N49: J14.pin2, IC6.Out_4_(_Controlled_by_Enable_2_)
  N50: IC5.Enable_1, IC5.Enable_2, WeMos_D1_Mini1.D1
  N51: IC5.In_1, IC5.In_4, WeMos_D1_Mini1.D2
  N52: IC5.In_2, IC5.In_3
  N53: IC5.+Vmotor, J15.pin2
  N54: IC5.+V, WeMos_D1_Mini1.3V3
  N55: IC6.Enable_1, IC6.Enable_2, WeMos_D1_Mini1.D4
  N56: IC6.In_1, IC6.In_4, WeMos_D1_Mini1.D0
  N57: IC6.0V, J15.pin1
  N58: IC6.In_2, WeMos_D1_Mini1.A0

notes:
  Motor 1
  Motor 2
  Motor 3
  Motor 4
  Ext_power

custom parts:
  JST XH 2A male: JST XH-2A
